# Fritzing sketch Trail Counter SD (saved by Fritzing 0.9.4)
breadboards: 1

parts:
  Part2 = Arduino Nano (Rev3.0)
  LCM1602_IIC1 = LCM1602 IIC [part_number="LCM1602 IIC" chip_label="LCM1602 IIC" package="DIP (Dual Inline) [THT]"]
  LCD1 = LCD screen
  ZS-042_RTC2 = ZS-042 RTC Module
  microSD1 = MicroSD Card Module
  KY-008_Laserdiode1 = Laser [part_number=1219301 package=keys]
  Mod1 = laser receiver [package=THT]

nets:
  GND: Part2.GND, LCM1602_IIC1.GND, ZS-042_RTC2.GND, microSD1.GND, KY-008_Laserdiode1.connector2pin, Mod1.pin1
  N1: Part2.D3, Mod1.pin2
  N2: Part2.D4, KY-008_Laserdiode1.connector0pin
  N3: Part2.D10, microSD1.CS
  N4: Part2.D11/MOSI, microSD1.MOSI
  N5: Part2.D12/MISO, microSD1.MISO
  VCC: Part2.VIN, LCM1602_IIC1.VCC, ZS-042_RTC2.VCC, microSD1.VCC, Mod1.pin3
  N6: Part2.A5, LCM1602_IIC1.SCL, ZS-042_RTC2.SCL
  N7: Part2.A4, LCM1602_IIC1.SDA, ZS-042_RTC2.SDA
  N8: Part2.D13/SCK, microSD1.SCK
  VSS: LCM1602_IIC1.VSS, LCD1.VSS
  VDD: LCM1602_IIC1.VDD, LCD1.VDD
  N9: LCM1602_IIC1.V0, LCD1.V0
  N10: LCM1602_IIC1.RS, LCD1.RS
  N11: LCM1602_IIC1.RW, LCD1.R/W
  N12: LCM1602_IIC1.E, LCD1.E
  N13: LCM1602_IIC1.D0, LCD1.DB0
  N14: LCM1602_IIC1.D1, LCD1.DB1
  N15: LCM1602_IIC1.D2, LCD1.DB2
  N16: LCM1602_IIC1.D3, LCD1.DB3
  N17: LCM1602_IIC1.D4, LCD1.DB4
  N18: LCM1602_IIC1.D5, LCD1.DB5
  N19: LCM1602_IIC1.D6, LCD1.DB6
  N20: LCM1602_IIC1.D7, LCD1.DB7
  N21: LCM1602_IIC1.A, LCD1.LED+
  N22: LCM1602_IIC1.K, LCD1.LED-

custom parts:
  LCM1602 IIC: I2C-Module to use a 1602 or 2004 LCD on with the wire.h libory Serial LCD Modul
  Laser: KEYES KY-008 650nm Laser Transmitter Module
  laser receiver: Generic non modulated laser receiver module.

// code stored in the sketch: trailcounter_push_button.ino
/*
  Displays Number of triggers from pushbutton to a 16x2 Display

  The circuit:
 * LCD RS pin to digital pin 12
 * LCD Enable pin to digital pin 11
 * LCD D4 pin to digital pin 5
 * LCD D5 pin to digital pin 4
 * LCD D6 pin to digital pin 3
 * LCD D7 pin to digital pin 2
 * LCD R/W pin to ground
 * LCD VSS pin to ground
 * LCD VCC pin to 5V
 * 10K resistor:
 * ends to +5V and ground
 * wiper to LCD VO pin (pin 3)

 Library originally added 18 Apr 2008
 by David A. Mellis
 library modified 5 Jul 2009
 by Limor Fried (http://www.ladyada.net)
 example added 9 Jul 2009
 by Tom Igoe
 modified 22 Nov 2010
 by Tom Igoe
 modified 7 Nov 2016
 by Arturo Guadalupi

 This example code is in the public domain.

 

*/

// include the library code:
#include <LiquidCrystal.h>

// initialize the library by associating any needed LCD interface pin
// with the arduino pin number it is connected to
const int rs = 7, en = 8, d4 = 9, d5 = 10, d6 = 11, d7 = 12, pushButton = 2;
LiquidCrystal lcd(rs, en, d4, d5, d6, d7);

int count = 0;
int lastCount = 0;
int buttonState = LOW;
int lastButtonState = LOW;
unsigned long lastDebounceTime = 0;  // the last time the output pin was toggled
unsigned long debounceDelay = 50;    // the debounce time; increase if the output flickers


void setup() {
   // initialize serial communication at 9600 bits per second:
  Serial.begin(9600);
  // make the pushbutton's pin an input:
  pinMode(pushButton, INPUT);

  // set up the LCD's number of columns and rows:
  lcd.begin(16, 2);
  // Print a message to the LCD.
  lcd.print("BONC Trail Count");
}

void loop() {
  // set the cursor to column 0, line 1
  // (note: line 1 is the second row, since counting begins with 0):
 
 
 
   int reading = digitalRead(pushButton);
  
  if (reading != lastButtonState)  {
    // reset the debouncing timer
    lastDebounceTime = millis();
  }
   if((millis() - lastDebounceTime) > debounceDelay) {
    // whatever the reading is at, it's been there for longer than the debounce
    // delay, so take it as the actual current state:

    // if the button state has changed:
    if (reading != buttonState) {
      buttonState = reading;

      // only toggle the LED if the new button state is HIGH
      if (buttonState == HIGH) {
         //increase count
    count++;
    
    lcd.setCursor(0, 1);

 
     if(count<2){ 
      lcd.print(count);
     
      lcd.print(" User");
     }
     else{
       lcd.print(count);
     
      lcd.print(" Users");
      delay(5);
     }
     }
   
    }
  }
 
  lastButtonState = reading;
 
}

// code stored in the sketch: trailcounter_push_button_I2C.ino
// include the  I2C library code and Wire.h:
#include <LiquidCrystal_I2C.h>
#include <Wire.h> 
//SCL to A5 and SDA to A4


LiquidCrystal_I2C lcd(0x27, 16, 2);
//set pin 2 to read button
const int pushButton = 2;
int count = 0;
int lastCount = 0;
int buttonState = LOW;
int lastButtonState = LOW;
unsigned long lastDebounceTime = 0;  // the last time the output pin was toggled
unsigned long debounceDelay = 50;    // the debounce time; increase if the output flickers


void setup() 
{
  // initialize the LCD
  lcd.begin();
  //turn on backlight
  lcd.backlight();
    // make the pushbutton's pin an input:
   pinMode(pushButton, INPUT);
   // initialize serial communication at 9600 bits per second:
  Serial.begin(9600);
  // Print a message to the LCD.
  lcd.print("BONC Trail Count");
}

void loop() 
{
    int reading = digitalRead(pushButton);
  
  if (reading != lastButtonState)  {
    // reset the debouncing timer
    lastDebounceTime = millis();
  }
   if((millis() - lastDebounceTime) > debounceDelay) {
    // whatever the reading is at, it's been there for longer than the debounce
    // delay, so take it as the actual current state:

    // if the button state has changed:
    if (reading != buttonState) {
      buttonState = reading;

      // only toggle the LED if the new button state is HIGH
      if (buttonState == HIGH) {
         //increase count
    count++;
    
    lcd.setCursor(0,1);

 
     if(count<2){ 
      lcd.print(count);
     
      lcd.print(" User");
     }
     else{
       lcd.print(count);
     
      lcd.print(" Users");
      delay(5);
     }
     Serial.print(count);
     }
   
    }
  }
 
  lastButtonState = reading;
 
}
